# Fritzing sketch Creeper_Schematic (saved by Fritzing 0.7.12b)
breadboards: 1

parts:
  LED2 = LED - 5mm [color="Blue (525nm)" package="5 mm [THT]"]
  LED4 = LED - 5mm [color="Blue (525nm)" package="5 mm [THT]"]
  S1 = Pushbutton [package="[THT]"]
  J1 = female pin header, 1 pin [form="♀ (female)"]
  J2 = female pin header, 1 pin [form="♀ (female)"]
  J3 = female pin header, 1 pin [form="♀ (female)"]
  U1 = attiny85 [package=dip]
  R6 = Resistor [tolerance=±5% resistance=220 package=THT]
  J5 = female pin header, 1 pin [form="♀ (female)"]
  J6 = female pin header, 1 pin [form="♀ (female)"]

nets:
  N1: LED2.cathode, LED4.cathode, J1.pin1, U1.Pin_4, R6.Pin_0, J5.pin1
  N2: LED2.anode, U1.Pin_5
  N3: LED4.anode, U1.Pin_6
  N4: S1.Pin_1, S1.Pin_2, U1.Pin_7, R6.Pin_1
  N5: S1.Pin_3, S1.Pin_4, J2.pin1, U1.Pin_8, J6.pin1
  N6: J3.pin1, U1.Pin_2
